# Fritzing sketch aio_sensor_1 (saved by Fritzing 0.9.10b)
circuit board: 8.46667cm x 5.64444cm
breadboards: 1

parts:
  OLED = Grove OLED 128x96
  WeMos_D1_Mini1 = WeMos D1 Mini
  DHT22 = DHT22 Humidity and Temperature Sensor
  S1 = Pushbutton [package="[THT]"]
  R1 = Resistor [tolerance=±5% power=0.25 resistance=220 package=THT]
  MQ-3 = MQ-3 breakout

nets:
  GND: OLED.GND, WeMos_D1_Mini1.G, DHT22.GND, S1.Pin_1, S1.Pin_2, MQ-3.GND
  VCC: OLED.VCC, WeMos_D1_Mini1.3V3
  N1: OLED.SDA, WeMos_D1_Mini1.D2
  N2: OLED.SCL, WeMos_D1_Mini1.D1
  5V: WeMos_D1_Mini1.5V, MQ-3.VCC
  N3: WeMos_D1_Mini1.A0, MQ-3.AO
  N4: WeMos_D1_Mini1.D5, DHT22.DATA, R1.Pin_1
  N5: WeMos_D1_Mini1.D6, S1.Pin_3, S1.Pin_4
  N6: DHT22.VDD, R1.Pin_0

custom parts:
  MQ-3 breakout: Alcohol sensor is capable of detecting alcohol (ethanol) particles on itself and gives the information in digital form back to us to manipulate with it. SKU:101251 • Voltage: 5V DC • Power: max 750mW • Measurement range: 0.04-4mg/L
